# Fritzing sketch EngineRoomGuard (saved by Fritzing 0.9.9b)
circuit board: 7.6cm x 8.5cm

parts:
  LED1 = LED - 5mm [color="Red (633nm)" current=0.030 package="5 mm [THT]"]
  C1 = Electrolytic Capacitor [capacitance=0.47mF voltage=35V package="100 mil [THT, electrolytic]"]
  C2 = Electrolytic Capacitor [capacitance=0.47mF voltage=35V package="100 mil [THT, electrolytic]"]
  D1 = Schottky Diode [part_number=1N5817 package="300 mil [THT]"]
  R1 = Resistor [tolerance=±5% power=0.25 resistance=330 package=THT]
  U2_Alarm = RELAY-SIL05-1A72-71D [part_number=SIL05-1A package=relay-g5v]
  U3_Smoke = RELAY-SIL05-1A72-71D [part_number=SIL25-1A package=relay-g5v]
  U4_Eng_1_Oil = RELAY-SIL05-1A72-71D [part_number=SIL24-1A package=relay-g5v]
  U5_Eng_2_Oil = RELAY-SIL05-1A72-71D [part_number=SIL24-1A package=relay-g5v]
  R2 = Resistor [tolerance=±5% power=0.25 resistance=4.7k package=THT]
  J3_Int_Piezo = Screw terminal - 2 pins [package=THT]
  U6_Gas = RELAY-SIL05-1A72-71D [part_number=SIL24-1A package=relay-g5v]
  IC1 = Voltage Regulator [part_number=7805 package=to220-igo]
  LED2 = LED - 5mm [color="Red (633nm)" current=0.030 package="5 mm [THT]"]
  R3 = Resistor [tolerance=±5% power=0.25 resistance=220 package=THT]
  J2 = screw terminal, 14 pins
  J1 = screw terminal, 14 pins
  U2 = LuaNode32 / ESP32 [part_number=ESP32S-PIN30]

nets:
  GND: LED1.cathode, C1.-, C2.-, U2_Alarm.COUT, U3_Smoke.IN, U4_Eng_1_Oil.IN, U5_Eng_2_Oil.IN, J3_Int_Piezo.pin2, U6_Gas.IN, IC1.GND, R3.Pin_0, J2.pin1, J2.pin4, J2.pin7, J2.pin9, J2.pin13, J1.pin3, J1.pin13, U2.GND
  N1: LED1.anode, R1.Pin_1
  N2: C1.+, D1.cathode, U2_Alarm.IN, IC1.IN
  N3: C2.+, R1.Pin_0, IC1.OUT, J2.pin14, U2.Vin
  N4: D1.anode, J1.pin14
  N5: U2_Alarm.CIN, U2.D19
  N6: U2_Alarm.OUT, J2.pin10
  N7: U3_Smoke.CIN, J1.pin12
  N8: U3_Smoke.COUT, J1.pin11
  N9: U3_Smoke.OUT, U2.D33
  N10: U4_Eng_1_Oil.CIN, J1.pin10
  N11: U4_Eng_1_Oil.COUT, J1.pin9
  N12: U4_Eng_1_Oil.OUT, U2.D25
  N13: U5_Eng_2_Oil.CIN, J1.pin8
  N14: U5_Eng_2_Oil.COUT, J1.pin7
  N15: U5_Eng_2_Oil.OUT, U2.D32
  N16: R2.Pin_0, J2.pin3, J2.pin6, J1.pin4, U2.3V3
  N17: R2.Pin_1, J2.pin2, J2.pin5, J1.pin2, U2.D4
  N18: J3_Int_Piezo.pin1, U2.D18
  N19: U6_Gas.CIN, J1.pin6
  N20: U6_Gas.COUT, J1.pin5
  N21: U6_Gas.OUT, U2.D26
  N22: LED2.cathode, R3.Pin_1
  N23: LED2.anode, U2.D2
  N24: J2.pin8, U2.D23
  N25: J2.pin11, U2.D22
  N26: J2.pin12, U2.D21

notes:
  R1
  5V Pwr LED
  Int Buzzer
  U4 Eng 1 Oil
  U5 Eng 2 Oil
  U2 Alarm
  U3 Smoke
  U6 Gas
  Input pin 1
  R2
  Input pin 14
  Output pin 1
  Output pin 14
  EngineRoomGuard v4 2022
  Int LED
  R3
  D1

custom parts:
  RELAY-SIL05-1A72-71D: MEDER SIL05-1A72-71D RSコンポーネンツ 349-2884
  LuaNode32 / ESP32: New Image for LuaNode32 DOIT ESP32 DEVKIT V1. Base parts from LuaNode32 / ESP32 ESP32 based LuaNode32 by G.Noorlander DOIT Esp32 DevKit v1 (30 pins long, 11 pins width) by Werner Rothschopf (modified by vanepp Dec 2018)
